# Fritzing sketch breadboard (saved by Fritzing 0.9.3b)
breadboards: 1

parts:
  Teensy_3_1 = Teensy 3.1
  SEG1 = 7-Segment Bubble Display [part_number=COM-12710 package="DIP (Dual Inline) [THT]"]
  LED1 = LED - 3mm [color="Red (633nm)" package="3 mm [THT]"]
  S1 = Pushbutton [package="[SMD]"]
  Q1 = Basic FET N-Channel [package="TO220 [THT]"]
  Q2 = Basic FET N-Channel [package="TO220 [THT]"]
  Q3 = Basic FET N-Channel [package="TO220 [THT]"]
  Q4 = Basic FET N-Channel [package="TO220 [THT]"]
  R12 = Resistor [tolerance=±5% resistance=340 package=THT]
  R13 = Resistor [tolerance=±5% resistance=340 package=THT]
  R14 = Resistor [tolerance=±5% resistance=340 package=THT]
  R15 = Resistor [tolerance=±5% resistance=340 package=THT]
  R16 = Resistor [tolerance=±5% resistance=340 package=THT]
  R17 = Resistor [tolerance=±5% resistance=340 package=THT]
  R18 = Resistor [tolerance=±5% resistance=340 package=THT]
  R19 = Resistor [tolerance=±5% resistance=340 package=THT]
  R22 = Resistor [tolerance=±5% resistance=10k package=THT]
  R23 = Resistor [tolerance=±5% resistance=10k package=THT]
  R24 = Resistor [tolerance=±5% resistance=1k package=THT]
  R25 = Resistor [tolerance=±5% resistance=1k package=THT]
  R26 = Resistor [tolerance=±5% resistance=1k package=THT]
  R27 = Resistor [tolerance=±5% resistance=1k package=THT]
  R20 = Resistor [tolerance=±5% resistance=10k package=THT]
  R21 = Resistor [tolerance=±5% resistance=10k package=THT]
  R28 = Resistor [tolerance=±5% resistance=340 package=THT]

nets:
  N1: Teensy_3_1.GND, LED1.anode, Q1.source, Q2.source, Q3.source, Q4.source, R22.Pin_0, R23.Pin_0, R20.Pin_1, R21.Pin_1
  N2: Teensy_3_1.D3, R19.Pin_1
  N3: Teensy_3_1.D4, R18.Pin_1
  N4: Teensy_3_1.D6, R16.Pin_1
  N5: Teensy_3_1.D7, R15.Pin_0
  N6: Teensy_3_1.D8, R14.Pin_1
  N7: Teensy_3_1.D9, R13.Pin_1
  N8: Teensy_3_1.D10, R12.Pin_0
  N9: Teensy_3_1.A6/D20, R26.Pin_1
  N10: Teensy_3_1.A7/D21, R25.Pin_1
  N11: Teensy_3_1.A8/D22, R24.Pin_1
  N12: Teensy_3_1.A9/D23, R27.Pin_1
  N13: Teensy_3_1.3V3, S1.Pin_3, S1.Pin_4
  N14: SEG1.C1, Q1.drain
  N15: SEG1.Ae, R15.Pin_1
  N16: SEG1.Ac, R17.Pin_1
  N17: SEG1.C3, Q3.drain
  N18: SEG1.Adp, R12.Pin_1
  N19: SEG1.C4, Q2.drain
  N20: SEG1.Ag, R13.Pin_0
  N21: SEG1.Ad, R16.Pin_0
  N22: SEG1.Af, R14.Pin_0
  N23: SEG1.C2, Q4.drain
  N24: SEG1.Ab, R18.Pin_0
  N25: SEG1.Aa, R19.Pin_0
  N26: LED1.cathode, R28.Pin_0
  N27: S1.Pin_1, S1.Pin_2
  N28: Q1.gate, R23.Pin_1, R26.Pin_0
  N29: Q2.gate, R27.Pin_0, R20.Pin_0
  N30: Q3.gate, R22.Pin_1, R25.Pin_0
  N31: Q4.gate, R24.Pin_0, R21.Pin_0

custom parts:
  7-Segment Bubble Display: This is the HP QDSP-6064 bubble display, a tiny, 4-digit, 7-segment numerical indicator. THis little guy is perfect if you need some user feedback from your system, but don’t want to fiddle with LCDs or other display options. The Bubble Display comes in an easy-to-use 12-pin DIP package and can be used in breadboards, protoboards, or PCBs.
